# Fritzing sketch schema (saved by Fritzing 0.9.3b)

parts:
  U1 = LuaNode32 / ESP32
  Součástka1 = Solar Cell
  Součástka2 = INA219 High Side DC Current Sensor Breakout [part_number=904]
  U4 = MPC1700 [package=sot23-3]
  C2 = Electrolytic Capacitor [capacitance=1000μF package="1010 [SMD, electrolytic]"]
  C3 = Capacitor [package=cap-pth-small2]
  Součástka3 = Adafruit SHT31-D Sensirion Temperature/Humidity Sensor [part_number="Adafruit #2857"]
  Součástka4 = Adafruit SHT31-D Sensirion Temperature/Humidity Sensor [part_number="Adafruit #2857"]
  Součástka5 = Adafruit SHT31-D Sensirion Temperature/Humidity Sensor [part_number="Adafruit #2857"]
  S1 = Reed switch [package=THT]
  S2 = Reed switch [package=THT]
  S3 = Reed switch [package=THT]
  VCC1 = Battery block 9V
  Součástka14 = INA219 High Side DC Current Sensor Breakout [part_number=904]
  S4 = Reed switch [package=THT]
  S5 = Reed switch [package=THT]
  S6 = Reed switch [package=THT]
  Solar_Charger_Liporider_-_Seeed_Studio1 = Solar Charger Liporider - Seeed Studio
  Q2 = Basic FET N-Channel [package="TO220 [THT]"]
  Součástka15 = Breakout Board for Electret Microphone
  Součástka16 = Breakout Board for Electret Microphone
  Součástka17 = Breakout Board for Electret Microphone

nets:
  N1: U1.EN, Q2.drain
  N2: U1.D35, Součástka15.AUD
  N3: U1.D32, Součástka16.AUD
  N4: U1.D33, Součástka17.AUD
  N5: U1.D25, S3.pin_1
  N6: U1.D26, S1.pin_1
  N7: U1.D27, S2.pin_1
  N8: U1.D14, S4.pin_1
  N9: U1.D13, S5.pin_1
  GND: U1.GND, Součástka2.GND, U4.GND, C2.-, C3.1, Součástka3.GND, Součástka4.GND, Součástka5.GND, VCC1.-, Součástka14.GND, Solar_Charger_Liporider_-_Seeed_Studio1.nessun_nome#1, Q2.source, Součástka15.GND, Součástka16.GND, Součástka17.GND
  VCC: U1.3V3, Součástka2.VCC, U4.OUT, Součástka3.VIN, Součástka4.VIN, Součástka5.VIN, S1.pin_2, S2.pin_2, S3.pin_2, Součástka14.VCC, S4.pin_2, S5.pin_2, S6.pin_2, Součástka15.VCC, Součástka16.VCC, Součástka17.VCC
  N10: U1.D2, Q2.gate
  N11: U1.D4, Součástka5.ADDR
  N12: U1.RX2, Součástka4.ADDR, Součástka4.RST
  N13: U1.TX2, Součástka3.ADDR
  N14: U1.D18, S6.pin_1
  N15: U1.D21, Součástka1.+, Součástka2.VIN+, Součástka2.SDA, Součástka3.SDA, Součástka4.SDA, Součástka5.SDA, Součástka14.VIN-, Součástka14.SDA, Solar_Charger_Liporider_-_Seeed_Studio1.nessun_nome#2
  N16: U1.D22, Součástka2.VIN-, Součástka2.SCL, Součástka3.SCL, Součástka4.SCL, Součástka5.SCL, Součástka14.SCL, Solar_Charger_Liporider_-_Seeed_Studio1.nessun_nome#6
  N17: Součástka1.-, Solar_Charger_Liporider_-_Seeed_Studio1.nessun_nome#5
  N18: U4.IN, C2.+, C3.2, VCC1.+, Součástka14.VIN+

notes:
  12V solar panel
  4.2V LiIon battery
  4.2V -> 3.3V
  Magnetic lock sensors
  INA219 sensors
  SHT31 temperature/humidity sensors
  IRF520N
  ESP32-WROOM-32U
  12V MPPT Solar Panel Controller for Lithium Li-ion 18650 Battery
  3X GY MAX4466 Microphone

custom parts:
  LuaNode32 / ESP32: ESP32 based LuaNode32
  INA219 High Side DC Current Sensor Breakout: This breakout board will solve all your power-monitoring problems. Instead of struggling with two multimeters, you can just use the handy INA219B chip on this breakout to both measure both the high side voltage and DC current draw over I2C with 1% precision. Most current-measuring devices such as our current panel meter are only good for low side measuring. That means that unless you want to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
  MPC1700: Small package LDO
  Adafruit SHT31-D Sensirion Temperature/Humidity Sensor: Sensirion Temperature/Humidity sensors are some of the finest & highest-accuracy devices you can get. And, finally we have some that have a true I2C interface for easy reading. The SHT31-D sensor has an excellent ±2% relative humidity and ±0.3°C accuracy for most uses. Unlike earlier SHT sensors, this sensor has a true I2C interface, and (bonus!) even with two address options. It also is 3V or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
